# Fritzing sketch graffiti-drone (saved by Fritzing 0.9.0b)

parts:
  Wifi_Redback_(Arduino_Mini-like) = Arduino Mini (Rev5)
  R1 = Resistor [tolerance=±5% resistance=220 package=THT]
  D1 = Rectifier Diode [part_number=1N4001 package="300 mil [THT]"]
  HCNE1-0520 = Solenoid
  HC-SR04_R = SRF05 Ultrasonic Rangefinder
  HC-SR04_L = SRF05 Ultrasonic Rangefinder
  IRLZ44 = Basic FET P-Channel [package="TO220 [THT]"]
  AR_Drone_battery = Power plug
  TSR-2450 = Voltage Regulator - 5V [package="TO220 [THT]"]

nets:
  N1: Wifi_Redback_(Arduino_Mini-like).D3_PWM, R1.Pin_1
  N2: Wifi_Redback_(Arduino_Mini-like).D4, HC-SR04_R.Echo
  N3: Wifi_Redback_(Arduino_Mini-like).D5_PWM, HC-SR04_R.Trig
  N4: Wifi_Redback_(Arduino_Mini-like).D6_PWM, HC-SR04_L.Echo
  N5: Wifi_Redback_(Arduino_Mini-like).D7, HC-SR04_L.Trig
  VCC: Wifi_Redback_(Arduino_Mini-like).VCC, HC-SR04_R.VCC, HC-SR04_L.VCC
  GND: Wifi_Redback_(Arduino_Mini-like).GND, HC-SR04_R.GND, HC-SR04_L.GND, IRLZ44.drain, AR_Drone_battery.GND, TSR-2450.GND
  N6: Wifi_Redback_(Arduino_Mini-like).5V, TSR-2450.output_voltage
  N7: R1.Pin_0, IRLZ44.gate
  N8: D1.cathode, HCNE1-0520.pin2, AR_Drone_battery.VCC, TSR-2450.input_voltage
  N9: D1.anode, HCNE1-0520.pin1, IRLZ44.source
